# Fritzing sketch Zany80 (saved by Fritzing 0.9.3b)
circuit board: 16.3315cm x 6.08828cm
breadboards: 1
perfboards: 1

parts:
  IC1 = Z80 A [package="DIP (Dual Inline) [THT]"]
  U1 = Voltage Regulator - 5V [package="TO220 [THT]"]
  VCC1 = Battery block 9V
  U6 = mystery part, 2 pins [chip_label=74HCT04]
  R1 = Resistor [tolerance=±5% resistance=1M package=THT]
  U7 = mystery part, 2 pins [chip_label=74HCT04]
  XTAL1 = Crystal [frequency="8 MHz" package=THT]
  R2 = Resistor [tolerance=±5% resistance=1k package=THT]
  C1 = Ceramic Capacitor [capacitance=22pF package="100 mil [THT, multilayer]"]
  C2 = Ceramic Capacitor [capacitance=22pF package="100 mil [THT, multilayer]"]
  J1 = rounded female pin header, 16 pins [form="♀ (female rounded)"]

nets:
  N1: IC1.A11, J1.pin5
  N2: IC1.A12, J1.pin4
  N3: IC1.A13, J1.pin3
  N4: IC1.A14, J1.pin2
  N5: IC1.A15, J1.pin1
  N6: IC1.CLK, U6.pin2
  N7: IC1.+5V, U1.output_voltage
  GND: IC1.GND, U1.GND, VCC1.-, C1.0, C2.0
  N8: IC1.A0, J1.pin16
  N9: IC1.A1, J1.pin15
  N10: IC1.A2, J1.pin14
  N11: IC1.A3, J1.pin13
  N12: IC1.A4, J1.pin12
  N13: IC1.A5, J1.pin11
  N14: IC1.A6, J1.pin10
  N15: IC1.A7, J1.pin9
  N16: IC1.A8, J1.pin8
  N17: IC1.A9, J1.pin7
  N18: IC1.A10, J1.pin6
  N19: U1.input_voltage, VCC1.+
  N20: U6.pin1, R1.Pin_1, U7.pin2, R2.Pin_1
  N21: R1.Pin_0, U7.pin1, XTAL1.pin_0, C1.1
  N22: XTAL1.pin_1, R2.Pin_0, C2.1

custom parts:
  Z80 A: Zilog Z80 A CPU
